# Fritzing sketch GalileosFinger (saved by Fritzing 0.9.2b)
breadboards: 1

parts:
  Parte1 = Arduino Nano (Rev3.0)
  Parte2 = EasyDriver_v44
  Parte3 = EasyDriver_v44
  M1 = Stepper Motor - Bipolar
  M2 = Stepper Motor - Bipolar
  R1 = Resistor [tolerance=±5% resistance=220 package=THT]
  Q1 = NPN-Transistor [package="TO92 [THT]"]
  LED1 = LED - 5mm [color="Red (633nm)" package="5 mm [THT]"]

nets:
  GND: Parte1.GND, Parte2.GND, Parte3.GND, Q1.C
  N1: Parte1.D4, Parte3.DIR
  N2: Parte1.D5, Parte3.STEP
  N3: Parte1.D6, Parte2.DIR
  N4: Parte1.D7, Parte2.STEP
  N5: Parte1.D12/MISO, R1.Pin_0, R1.Pin_1, Q1.B
  VCC: Parte1.5V, Parte2.VCC, Parte3.VCC
  N6: Parte1.3V3, LED1.anode
  N7: Parte2.OUT2A, M1.A
  N8: Parte2.OUT2B, M1.C
  N9: Parte2.OUT1A, M1.B
  N10: Parte2.OUT1B, M1.D
  N11: Parte3.OUT2A, M2.A
  N12: Parte3.OUT2B, M2.C
  N13: Parte3.OUT1A, M2.B
  N14: Parte3.OUT1B, M2.D
  N15: Q1.E, LED1.cathode
